# Fritzing sketch NanoPCB (saved by Fritzing 0.9.3b)
circuit board: 6.6cm x 5.3cm
breadboards: 1

parts:
  Arduino_nano = Arduino Nano (Rev3.0)
  Sensor_1 = Dagu DGServo 9g header (male) [package=THT]
  Sensor_2 = Dagu DGServo 9g header (male) [package=THT]
  Sensor_3 = Dagu DGServo 9g header (male) [package=THT]
  Sensor_4 = Dagu DGServo 9g header (male) [package=THT]
  Relays = female pin header, 6 pins [form="♀ (female)"]
  J1 = Camdenboss CTB0158-2 [part_number=CTB0158-2 package=THT]
  R1 = Resistor [tolerance=±5% resistance=220 package="0805 [SMD]"]
  D1 = LTE-302 [package=lte-302]

nets:
  GND: Arduino_nano.GND, Sensor_1.gnd, Sensor_2.gnd, Sensor_3.gnd, Sensor_4.gnd, Relays.pin1, J1.pin2, D1.C
  N1: Arduino_nano.D5, R1.Pin_1
  N2: Arduino_nano.D9, Relays.pin3
  N3: Arduino_nano.D10, Relays.pin4
  N4: Arduino_nano.D11/MOSI, Relays.pin5
  N5: Arduino_nano.D12/MISO, Relays.pin6
  N6: Arduino_nano.VIN, J1.pin1
  VCC: Arduino_nano.5V, Sensor_1.Vcc, Sensor_2.Vcc, Sensor_3.Vcc, Sensor_4.Vcc, Relays.pin2
  N7: Arduino_nano.A3, Sensor_1.pulse
  N8: Arduino_nano.A2, Sensor_2.pulse
  N9: Arduino_nano.A1, Sensor_3.pulse
  N10: Arduino_nano.A0, Sensor_4.pulse
  N11: R1.Pin_0, D1.A
